# Fritzing sketch MagicClock (saved by Fritzing 1.0.2b)
circuit board: 6.00909cm x 4.67326cm
breadboards: 1

parts:
  U1 = ESP32-38PinWide [part_number=ESP32-38PinWide]
  J1 = Basic Servo
  R1 = Resistor [tolerance=±5% power=0.25W resistance=1k package=THT]
  R2 = Resistor [tolerance=±5% power=0.25W resistance=1k package=THT]
  LED1 = LED - 5mm [color="Red (633nm)" current=0.030A package="5 mm [THT]"]
  LED2 = LED - 5mm [color="Green (560nm)" current=0.030A package="5 mm [THT]"]
  S2 = Pushbutton [package="[THT]"]
  S1 = Pushbutton [package="[THT]"]

nets:
  N1: U1.GPIO33, S2.Pin_3, S2.Pin_4
  N2: U1.GPIO25, S1.Pin_3, S1.Pin_4
  N3: U1.GPIO26, R2.Pin_0
  N4: U1.GPIO27, R1.Pin_0
  GND: U1.GND, J1.gnd, LED1.cathode, LED2.cathode, S2.Pin_1, S2.Pin_2, S1.Pin_1, S1.Pin_2
  N5: U1.GPIO13, J1.pulse
  VIN: U1.VIN, J1.vcc
  N6: R1.Pin_1, LED1.anode
  N7: R2.Pin_1, LED2.anode

custom parts:
  ESP32-38PinWide: Generic 38-Pin ESP32 with wide format (only access to one side of pins on a breadboard) based on Stephen Lilley's HiLetgo ESP-WROOM-32 ESP32 ESP-32S Development Board.
